# Fritzing sketch LDR_LED (saved by Fritzing 0.8.0b)
breadboards: 1

parts:
  Parte1 = Arduino Uno (Rev3)
  R1 = Photocell (LDR) [package=THT]
  R2 = Resistor [tolerance=±5% resistance=220 package="0805 [SMD]"]
  LED1 = LED - 3mm [color="Red (633nm)" package="3 mm [THT]"]  # not connected

nets:
  N1: Parte1.A0, R1.pin_0, R2.Pin_1
  N2: Parte1.GND, R2.Pin_0
  N3: Parte1.5V, R1.pin_1

notes:
  220 Ohm
