# Fritzing sketch fotometro (saved by Fritzing 0.7.10b)
breadboards: 1

parts:
  R1 = Photocell (LDR) [package=THT]
  R2 = Resistor [tolerance=±5% resistance=10k package=THT]
  Arduino1 = Arduino
  LED1 = LED - 5mm [color="Red (633nm)" package="5 mm [THT]"]
  LED2 = LED - 5mm [color="Red (633nm)" package="5 mm [THT]"]
  LED3 = LED - 5mm [color="Red (633nm)" package="5 mm [THT]"]
  LED4 = LED - 5mm [color="Red (633nm)" package="5 mm [THT]"]
  LED5 = LED - 5mm [color="Red (633nm)" package="5 mm [THT]"]

nets:
  N1: R1.pin_0, Arduino1.+5V
  N2: R1.pin_1, R2.Pin_0, Arduino1.A0
  N3: R2.Pin_1, Arduino1.GND, LED1.cathode, LED2.cathode, LED3.cathode, LED4.cathode, LED5.cathode
  N4: Arduino1.D6, LED1.anode
  N5: Arduino1.D5, LED2.anode
  N6: Arduino1.D4, LED3.anode
  N7: Arduino1.D3, LED4.anode
  N8: Arduino1.D2, LED5.anode
